# Fritzing sketch ir_transmitter (saved by Fritzing 0.9.2b)
breadboards: 1

parts:
  Часть1 = Arduino Nano (Rev3.0)
  DS1 = DS18B20 1-Wire Temperature Sensor [part_number=DS18B20]
  R1 = Resistor [tolerance=±5% resistance=4.7k package=THT]
  LED1 = LED - 5mm [color="Infrared (940nm)" package="5 mm [THT]"]
  R2 = Resistor [tolerance=±5% resistance=1 package=THT]
  R3 = Resistor [tolerance=±5% resistance=1k package=THT]
  Q2 = NPN-Transistor [part_number=BC547 package="TO92 [THT]"]

nets:
  GND: Часть1.GND, DS1.GND, Q2.E
  N1: Часть1.D6, R3.Pin_1
  N2: Часть1.D8, DS1.DQ, R1.Pin_0
  5V: Часть1.5V, DS1.VDD, R1.Pin_1, LED1.cathode
  N3: LED1.anode, R2.Pin_0
  N4: R2.Pin_1, Q2.C
  N5: R3.Pin_0, Q2.B
